// Logisim project carryahead.circ as structural Verilog: 1 circuit, main circuit main
module main (
  input  C0,
  input  [3:0] in_2,
  input  [3:0] in_3
);

  wire and_1_out, and_2_out, and_3_out, and_4_out, and_5_out, and_6_out, and_7_out, and_8_out, and_9_out,
       and_10_out, C1_out, G0_out, G1_out, G2_out, G3_out, or_1_out, or_2_out, P0_out, P1_out, P2_out,
       P3_out, xor_2_out, xor_3_out, xor_4_out;
  wire [0:0] or_3_out;
  wire [3:0] xor_1_out;

  Hex_Digit_Display hex_digit_display_1 (.value(in_2));  // open: dp
  Hex_Digit_Display hex_digit_display_2 (.value(in_3));  // open: dp
  and G0 (G0_out, in_2[0], in_3[0]);
  xor P0 (P0_out, in_2[0], in_3[0]);
  and G1 (G1_out, in_2[1], in_3[1]);
  xor P1 (P1_out, in_2[1], in_3[1]);
  and G2 (G2_out, in_2[2], in_3[2]);
  xor P2 (P2_out, in_2[2], in_3[2]);
  and G3 (G3_out, in_2[3], in_3[3]);
  xor P3 (P3_out, in_2[3], in_3[3]);
  and and_1 (and_1_out, C0, P0_out);
  and and_2 (and_2_out, G0_out, P1_out);
  and and_3 (and_3_out, P1_out, P0_out, C0);
  and and_4 (and_4_out, G1_out, P2_out);
  and and_5 (and_5_out, P2_out, P1_out, G0_out);
  and and_6 (and_6_out, P2_out, P1_out, P0_out, C0);
  and and_7 (and_7_out, P3_out, G2_out);
  and and_8 (and_8_out, P3_out, P2_out, G1_out);
  and and_9 (and_9_out, P3_out, P2_out, P1_out, G0_out);
  and and_10 (and_10_out, P3_out, G0_out, P1_out, P0_out, C0);
  ExactlyOne xor_1 (.out(xor_1_out[0]), .in0(C0), .in1(in_2[0]), .in2(in_3[0]));
  or C1 (C1_out, G0_out, and_1_out);
  or or_1 (or_1_out, G1_out, and_2_out, and_3_out);
  or or_2 (or_2_out, G2_out, and_4_out, and_5_out, and_6_out);
  or or_3 (or_3_out[0], and_7_out, G3_out, and_8_out, and_9_out, and_10_out);
  xor xor_2 (xor_2_out, in_2[1], in_3[1]);
  xor xor_3 (xor_3_out, in_2[2], in_3[2]);
  xor xor_4 (xor_4_out, in_2[3], in_3[3]);
  xor xor_5 (xor_1_out[1], C1_out, xor_2_out);
  xor xor_6 (xor_1_out[2], or_1_out, xor_3_out);
  xor xor_7 (xor_1_out[3], or_2_out, xor_4_out);
  Hex_Digit_Display hex_digit_display_3 (.value({3'b000, or_3_out[0]}));  // open: dp
  Hex_Digit_Display hex_digit_display_4 (.value(xor_1_out));  // open: dp
endmodule
